# Fritzing sketch Project10 Fritzing (saved by Fritzing 0.9.0b)
breadboards: 1

parts:
  Part1 = Arduino Uno (Rev3)
  DHT11 = DHT11 Humitidy and Temperature Sensor
  R3 = Resistor [tolerance=±5% resistance=10k package=THT]

nets:
  GND: Part1.GND, DHT11.GND
  N1: Part1.D2, DHT11.DATA, R3.Pin_0
  5V: Part1.5V, DHT11.VDD, R3.Pin_1

custom parts:
  DHT11 Humitidy and Temperature Sensor: DHT11 Humidity and Temperature Sensor
