# Fritzing sketch Project11 Fritzing (saved by Fritzing 0.9.1b)
breadboards: 1

parts:
  Part1 = Arduino Uno (Rev3)
  S1 = Momentary Switch [package=ksa_sealed_tac_switch]
  R2 = Resistor [tolerance=±5% resistance=10k package="0603 [SMD]"]
  LED2 = RGB LED - (4 legs) [package="5 mm [THT]"]
  PIR1 = PIR sensor
  J1 = Piezo Speaker
  R3 = Photocell (LDR) [package=THT]
  R4 = Resistor [tolerance=±5% resistance=10k package="0603 [SMD]"]
  LED3 = RGB LED - (4 legs) [package="5 mm [THT]"]
  R6 = Resistor [package="0402 [SMD]"]
  R7 = Resistor [package="0402 [SMD]"]
  R5 = Resistor [tolerance=±5% resistance=220 package=THT]
  R8 = Resistor [package="0402 [SMD]"]
  R9 = Resistor [package="0402 [SMD]"]

nets:
  N1: Part1.A5/SCL, R3.pin_1, R4.Pin_0
  N2: Part1.D8, PIR1.SIG
  N3: Part1.D9_PWM, R7.Pin_1
  N4: Part1.D10_PWM/SS, R6.Pin_1
  N5: Part1.D11_PWM/MOSI, R5.Pin_1
  N6: Part1.D2, S1.2, R2.Pin_0
  N7: Part1.D3_PWM, R9.Pin_1
  N8: Part1.D5_PWM, R8.Pin_1
  N9: Part1.D6_PWM, J1.pin2
  5V: Part1.5V, R2.Pin_1, LED2.common_anode, PIR1.VDD, R3.pin_0, LED3.common_anode
  GND: Part1.GND, S1.4, PIR1.GND, J1.pin1, R4.Pin_1
  N10: LED2.red_cathode, R8.Pin_0
  N11: LED2.blue_cathode, R9.Pin_0
  N12: LED3.red_cathode, R5.Pin_0
  N13: LED3.green_cathode, R6.Pin_0
  N14: LED3.blue_cathode, R7.Pin_0
