# Fritzing sketch Project5 Fritzing (saved by Fritzing 0.9.0b)
breadboards: 1

parts:
  Part1 = Arduino Uno (Rev3)
  R1 = Resistor [package="0402 [SMD]"]
  LED1 = smd LED [color="Red (633nm)" package="0805 [SMD]"]
  PIR1 = PIR sensor

nets:
  N1: Part1.D11_PWM/MOSI, R1.Pin_0
  N2: Part1.D2, PIR1.SIG
  5V: Part1.5V, PIR1.VDD
  GND: Part1.GND, LED1.cathode, PIR1.GND
  N3: R1.Pin_1, LED1.anode
