# Fritzing sketch Project6 Fritzing (saved by Fritzing 0.9.1b)
breadboards: 1

parts:
  Part1 = Arduino Uno (Rev3)
  R3 = Resistor [tolerance=±5% resistance=10k package=THT]
  LED2 = smd LED [color="Yellow (585nm)" package="0603 [SMD]"]
  LED3 = smd LED [color="Red (635nm)" package="0603 [SMD]"]
  R4 = Resistor [tolerance=±5% resistance=220 package="1206 [SMD]"]
  R5 = Resistor [tolerance=±5% resistance=220 package="1206 [SMD]"]
  R6 = Resistor [tolerance=±5% resistance=220 package="1206 [SMD]"]
  R7 = Photocell (LDR) [package=THT]
  LED1 = smd LED [color="Green (555nm)" package="0805 [SMD]"]
  LED4 = smd LED [color="Red (635nm)" package="0603 [SMD]"]
  LED5 = smd LED [color="Yellow (585nm)" package="0603 [SMD]"]
  LED6 = smd LED [color="Green (555nm)" package="0805 [SMD]"]
  R8 = Resistor [tolerance=±5% resistance=220 package="1206 [SMD]"]
  R9 = Resistor [tolerance=±5% resistance=220 package="1206 [SMD]"]
  R10 = Resistor [tolerance=±5% resistance=220 package="1206 [SMD]"]

nets:
  N1: Part1.A0, R3.Pin_0, R7.pin_1
  N2: Part1.D8, LED1.anode
  N3: Part1.D9_PWM, LED6.anode
  N4: Part1.D10_PWM/SS, LED2.anode
  N5: Part1.D11_PWM/MOSI, LED5.anode
  N6: Part1.D12/MISO, LED4.anode
  N7: Part1.D13/SCK, LED3.anode
  N8: Part1.GND, R3.Pin_1, R4.Pin_1, R5.Pin_1, R6.Pin_1, R8.Pin_1, R9.Pin_1, R10.Pin_1
  N9: Part1.5V, R7.pin_0
  N10: LED2.cathode, R8.Pin_0
  N11: LED3.cathode, R4.Pin_0
  N12: R5.Pin_0, LED4.cathode
  N13: R6.Pin_0, LED5.cathode
  N14: LED1.cathode, R10.Pin_0
  N15: LED6.cathode, R9.Pin_0
