# Fritzing sketch Project7 Fritzing (saved by Fritzing 0.9.1b)
breadboards: 1

parts:
  Part1 = Arduino Uno (Rev3)
  R4 = Resistor [package="0402 [SMD]"]
  R3 = Resistor [package="0402 [SMD]"]
  R1 = Resistor [package="0402 [SMD]"]
  LED2 = RGB LED - (4 legs) [package="5 mm [THT]"]
  R5 = Trimmer Potentiometer [maximum_resistance=10kΩ package=THT]

nets:
  N1: Part1.A0, R5.wiper
  N2: Part1.D9_PWM, R4.Pin_0
  N3: Part1.D10_PWM/SS, R3.Pin_0
  N4: Part1.D11_PWM/MOSI, R1.Pin_0
  N5: Part1.5V, LED2.common_anode, R5.leg1
  N6: Part1.GND, R5.leg2
  N7: R4.Pin_1, LED2.blue_cathode
  N8: R3.Pin_1, LED2.green_cathode
  N9: R1.Pin_1, LED2.red_cathode
