# Fritzing sketch Project7 Fritzing (saved by Fritzing 0.9.1b)
breadboards: 1

parts:
  Part1 = Arduino Uno (Rev3)
  S1 = Momentary Switch [package=ksa_sealed_tac_switch]
  R4 = Resistor [package="0402 [SMD]"]
  R3 = Resistor [package="0402 [SMD]"]
  R1 = Resistor [package="0402 [SMD]"]
  LED2 = RGB LED - (4 legs) [package="5 mm [THT]"]
  R2 = Resistor [tolerance=±5% resistance=10k package="0603 [SMD]"]

nets (from the breadboard view):
  N1: Part1.D9_PWM, R4.Pin_0
  N2: Part1.D10_PWM/SS, R3.Pin_0
  N3: Part1.D11_PWM/MOSI, R1.Pin_0
  N4: Part1.D2, S1.2, R2.Pin_0
  N5: Part1.5V, R2.Pin_1
  N6: Part1.GND, S1.4
  N7: R4.Pin_1, LED2.blue_cathode
  N8: R3.Pin_1, LED2.green_cathode
  N9: R1.Pin_1, LED2.red_cathode
