# Fritzing sketch Project8a Fritzing (saved by Fritzing 0.9.0b)
breadboards: 1

parts:
  Part1 = Arduino Uno (Rev3)
  PIR1 = PIR sensor
  J1 = Piezo Speaker

nets:
  N1: Part1.D9_PWM, J1.pin2
  N2: Part1.D2, PIR1.SIG
  5V: Part1.5V, PIR1.VDD
  GND: Part1.GND, PIR1.GND, J1.pin1
