# Fritzing sketch Project9 Fritzing (saved by Fritzing 0.9.1b)
breadboards: 1

parts:
  Part1 = Arduino Uno (Rev3)
  R1 = Resistor [package="0402 [SMD]"]
  LED2 = RGB LED - (4 legs) [package="5 mm [THT]"]
  R2 = Resistor [package="0402 [SMD]"]
  R3 = Resistor [package="0402 [SMD]"]

nets:
  N1: Part1.D9_PWM, R3.Pin_1
  N2: Part1.D10_PWM/SS, R2.Pin_1
  N3: Part1.D11_PWM/MOSI, R1.Pin_1
  N4: Part1.5V, LED2.common_anode
  N5: R1.Pin_0, LED2.red_cathode
  N6: LED2.green_cathode, R2.Pin_0
  N7: LED2.blue_cathode, R3.Pin_0
